// Logisim project cpu.circ as structural Verilog: 14 circuits, main circuit CPU
module only_ram (
  input  Interrupt
);

  wire clock_1_out, cpu_1_mr, cpu_1_mw;
  wire [7:0] ram_1_data;
  wire [15:0] cpu_1_a;

  Clock clock_1 (.out(clock_1_out));
  RAM #(.addrWidth(16), .databus("bidir")) ram_1 (
    .addr(cpu_1_a), .we(cpu_1_mr), .oe(cpu_1_mw), .clk(clock_1_out), .data(ram_1_data));
  CPU cpu_1 (
    .MR(cpu_1_mr), .MW(cpu_1_mw), .Do(ram_1_data), .A(cpu_1_a), .CLK(clock_1_out), .I(Interrupt),
    .D(ram_1_data));
endmodule

module seperate_mem (
  input  [15:0] in_1,
  input  in_2,
  input  in_3,
  input  Interrupt
);

  wire and_1_out, and_2_out, and_3_out, clock_1_out;
  wire [7:0] cpu_1_do, rom_1_data;

  Clock clock_1 (.out(clock_1_out));
  CPU cpu_1 (.Do(cpu_1_do), .CLK(clock_1_out), .I(Interrupt), .D(cpu_1_do));  // open: MR, MW, A
  and and_1 (and_1_out, ~in_1[15], in_2);  // AND_Gate
  and and_2 (and_2_out, in_3, ~in_1[15]);  // AND_Gate
  and and_3 (and_3_out, in_3, in_1[15]);
  RAM #(.addrWidth(15), .databus("bidir")) ram_1 (
    .addr(in_1[14:0]), .we(and_1_out), .oe(and_2_out), .clk(clock_1_out), .data(cpu_1_do));
  ROM #(.addrWidth(15)) rom_1 (.addr(in_1[14:0]), .data(rom_1_data));
  assign cpu_1_do = and_3_out ? rom_1_data : 8'bz;  // Controlled_Buffer controlled_buffer_1

  // Notes on the sheet:
  //   contents of rom_1 (hex, n*v repeats v):
  //   11
endmodule

// K8-16
module CPU (
  input  I,
  input  [7:0] D,
  input  CLK,
  output MR,
  output MW,
  output [7:0] Do,
  output [15:0] A
);

  wire alu_1_flags_cf_in, alu_1_flags_nf_in, alu_1_flags_zf_in, flags_1_cf_out, flags_1_if_out,
       flags_1_nf_out, flags_1_zf_out, mid_1_alu_add, mid_1_alu_and, mid_1_alu_asel, mid_1_alu_asr,
       mid_1_alu_bsel, mid_1_alu_inv, mid_1_alu_lsl, mid_1_alu_pa, mid_1_alu_pb, mid_1_alu_pbtoah,
       mid_1_cu_cnd, mid_1_cu_wcf, mid_1_cu_wif, mid_1_cu_wmd, mid_1_cu_wnf, mid_1_cu_wzf, mid_1_flags_if_in,
       mid_1_flags_rsel, mid_1_flags_wcf, mid_1_flags_wif, mid_1_flags_wnf, mid_1_flags_ws, mid_1_flags_wzf,
       mid_1_grf_r, mid_1_grf_sel_a, mid_1_grf_sel_b, mid_1_grf_sel_x, mid_1_grf_sel_y, mid_1_grf_w,
       mid_1_ip_inc_sel_iph, mid_1_ip_inc_sel_ipl, mid_1_rtmp_rg, mid_1_rtmp_rs, mid_1_rtmp_wa,
       mid_1_rtmp_wg, mid_1_rtmp_ws, mid_1_srf_r, mid_1_srf_sel_iph, mid_1_srf_sel_ipl, mid_1_srf_sel_md,
       mid_1_srf_sel_sph, mid_1_srf_sel_spl, mid_1_srf_w;
  wire [7:0] alu_1_res, ip_inc_1_ip8_out, rtmp_1_alu_btmp, rtmp_1_g_out, srf_1_cu_md, srf_1_ip_inc_ip8_in,
       srf_1_s_out;
  wire [11:0] cu_1_mc_rom_adr, mid_1_cu_nmip;
  wire [55:0] cu_1_mid_mi, mc_rom_1_mi;

  assign Do = MR ? D : 8'bz;  // Controlled_Buffer controlled_buffer_1
  // Probe on flags_1_if_out
  // Probe on flags_1_nf_out
  // Probe on flags_1_zf_out
  // Probe on flags_1_cf_out
  MID mid_1 (
    .CU_wcf(mid_1_cu_wcf), .CU_wzf(mid_1_cu_wzf), .CU_wnf(mid_1_cu_wnf), .CU_wif(mid_1_cu_wif),
    .GRF_sel_y(mid_1_grf_sel_y), .GRF_sel_x(mid_1_grf_sel_x), .GRF_sel_b(mid_1_grf_sel_b),
    .GRF_sel_a(mid_1_grf_sel_a), .CU_cnd(mid_1_cu_cnd), .CU_wmd(mid_1_cu_wmd), .CU_nmip(mid_1_cu_nmip),
    .SRF_sel_iph(mid_1_srf_sel_iph), .SRF_sel_ipl(mid_1_srf_sel_ipl), .SRF_sel_sph(mid_1_srf_sel_sph),
    .SRF_sel_spl(mid_1_srf_sel_spl), .SRF_sel_md(mid_1_srf_sel_md), .SRF_r(mid_1_srf_r), .SRF_w(mid_1_srf_w),
    .RAM_r(MR), .RAM_w(MW), .IP_INC_sel_iph(mid_1_ip_inc_sel_iph), .IP_INC_sel_ipl(mid_1_ip_inc_sel_ipl),
    .FLAGS_rsel(mid_1_flags_rsel), .FLAGS_ws(mid_1_flags_ws), .FLAGS_if_in(mid_1_flags_if_in),
    .FLAGS_wcf(mid_1_flags_wcf), .FLAGS_wzf(mid_1_flags_wzf), .FLAGS_wnf(mid_1_flags_wnf),
    .FLAGS_wif(mid_1_flags_wif), .ALU_bsel(mid_1_alu_bsel), .ALU_add(mid_1_alu_add), .ALU_and(mid_1_alu_and),
    .ALU_inv(mid_1_alu_inv), .ALU_asel(mid_1_alu_asel), .ALU_pbtoah(mid_1_alu_pbtoah), .ALU_pb(mid_1_alu_pb),
    .ALU_pa(mid_1_alu_pa), .ALU_asr(mid_1_alu_asr), .ALU_lsl(mid_1_alu_lsl), .rTMP_wg(mid_1_rtmp_wg),
    .rTMP_rg(mid_1_rtmp_rg), .rTMP_ws(mid_1_rtmp_ws), .rTMP_rs(mid_1_rtmp_rs), .rTMP_wa(mid_1_rtmp_wa),
    .GRF_w(mid_1_grf_w), .GRF_r(mid_1_grf_r), .mi(cu_1_mid_mi));
  // Probe on srf_1_cu_md
  CU cu_1 (
    .MID_mi(cu_1_mid_mi), .MC_ROM_adr(cu_1_mc_rom_adr), .nmip(mid_1_cu_nmip), .md(srf_1_cu_md),
    .MC_ROM_mi(mc_rom_1_mi), .wcf(mid_1_cu_wcf), .wzf(mid_1_cu_wzf), .wnf(mid_1_cu_wnf), .wif(mid_1_cu_wif),
    .cnd(mid_1_cu_cnd), .FLAGS_cf_out(flags_1_cf_out), .FLAGS_zf_out(flags_1_zf_out),
    .FLAGS_nf_out(flags_1_nf_out), .FLAGS_if_out(flags_1_if_out), .i(I), .sel_adr(mid_1_cu_wmd), .clock(CLK));
  SRF srf_1 (
    .s_out(srf_1_s_out), .IP_INC_ip8_in(srf_1_ip_inc_ip8_in), .CU_md(srf_1_cu_md), .w(mid_1_srf_w),
    .INC_sel(mid_1_ip_inc_sel_iph), .INC_sel_ipl(mid_1_ip_inc_sel_ipl), .IP_INC_ip8_out(ip_inc_1_ip8_out),
    .s_in(srf_1_s_out), .sel_iph(mid_1_srf_sel_iph), .sel_ipl(mid_1_srf_sel_ipl),
    .sel_sph(mid_1_srf_sel_sph), .sel_spl(mid_1_srf_sel_spl), .RAM_r(MR), .RAM_d_out(Do), .r(mid_1_srf_r),
    .sel_md(mid_1_srf_sel_md), .clock(CLK));
  IP_INC ip_inc_1 (
    .ip8_out(ip_inc_1_ip8_out), .sel_ipl(mid_1_ip_inc_sel_ipl), .sel_iph(mid_1_ip_inc_sel_iph),
    .ip8_in(srf_1_ip_inc_ip8_in), .clock(CLK));
  // Probe on cu_1_mc_rom_adr
  // Probe on mc_rom_1_mi
  // Probe on srf_1_s_out
  Pull_Resistor pull_resistor_1 (.node(srf_1_s_out));
  FLAGS flags_1 (
    .if_out(flags_1_if_out), .nf_out(flags_1_nf_out), .zf_out(flags_1_zf_out), .cf_out(flags_1_cf_out),
    .g(rtmp_1_g_out), .cf_in(alu_1_flags_cf_in), .nf_in(alu_1_flags_nf_in), .zf_in(alu_1_flags_zf_in),
    .if_in(mid_1_flags_if_in), .wif(mid_1_flags_wif), .wnf(mid_1_flags_wnf), .wzf(mid_1_flags_wzf),
    .wcf(mid_1_flags_wcf), .ws(mid_1_flags_ws), .rsel(mid_1_flags_rsel), .clock(CLK));
  MC_ROM mc_rom_1 (.mi(mc_rom_1_mi), .adr(cu_1_mc_rom_adr));
  ALU alu_1 (
    .res(alu_1_res), .adrl(A[7:0]), .FLAGS_zf_in(alu_1_flags_zf_in), .FLAGS_nf_in(alu_1_flags_nf_in),
    .FLAGS_cf_in(alu_1_flags_cf_in), .adrh(A[15:8]), .asel(mid_1_alu_asel), .ag(rtmp_1_g_out),
    .as(srf_1_s_out), .cf_in(flags_1_cf_out), .inv(mid_1_alu_inv), .btmp(rtmp_1_alu_btmp), .bs(srf_1_s_out),
    .bsel(mid_1_alu_bsel), .\and (mid_1_alu_and), .add(mid_1_alu_add), .pb(mid_1_alu_pb), .pa(mid_1_alu_pa),
    .pbtoah(mid_1_alu_pbtoah), .asr(mid_1_alu_asr), .lsl(mid_1_alu_lsl));
  // Probe on alu_1_res
  rTMP rtmp_1 (
    .ALU_btmp(rtmp_1_alu_btmp), .s_out(srf_1_s_out), .g_out(rtmp_1_g_out), .wg(mid_1_rtmp_wg),
    .rg(mid_1_rtmp_rg), .ws(mid_1_rtmp_ws), .rs(mid_1_rtmp_rs), .wa(mid_1_rtmp_wa), .g_in(rtmp_1_g_out),
    .s_in(srf_1_s_out), .ALU_res(alu_1_res), .clock(CLK));
  Pull_Resistor pull_resistor_2 (.node(rtmp_1_g_out));
  // Probe on rtmp_1_g_out
  GRF grf_1 (
    .g_out(rtmp_1_g_out), .g_in(rtmp_1_g_out), .sel_y(mid_1_grf_sel_y), .sel_x(mid_1_grf_sel_x),
    .sel_b(mid_1_grf_sel_b), .sel_a(mid_1_grf_sel_a), .r(mid_1_grf_r), .w(mid_1_grf_w), .clock(CLK));

  // Notes on the sheet:
  //   ADR_BUS
endmodule

module GRF (
  input  r,
  input  w,
  input  [7:0] g_in,
  input  sel_y,
  input  sel_x,
  input  sel_b,
  input  sel_a,
  input  clock,
  output [7:0] g_out
);

  wire and_1_out, and_2_out, and_3_out, and_4_out, and_5_out, and_6_out, and_7_out, and_8_out;
  wire [7:0] rA_q, rB_q, rX_q, rY_q;

  and and_1 (and_1_out, w, sel_y);
  and and_2 (and_2_out, w, sel_x);
  and and_3 (and_3_out, w, sel_b);
  and and_4 (and_4_out, w, sel_a);
  Register #(.trigger("high")) rY (.D(g_in), .en(and_1_out), .Q(rY_q), .clk(clock));  // open: clr
  Register #(.trigger("high")) rX (.D(g_in), .en(and_2_out), .Q(rX_q), .clk(clock));  // open: clr
  Register #(.trigger("high")) rB (.D(g_in), .en(and_3_out), .Q(rB_q), .clk(clock));  // open: clr
  Register #(.trigger("high")) rA (.D(g_in), .en(and_4_out), .Q(rA_q), .clk(clock));  // open: clr
  assign g_out = and_5_out ? rY_q : 8'bz;  // Controlled_Buffer controlled_buffer_1
  and and_5 (and_5_out, sel_y, r);
  assign g_out = and_6_out ? rX_q : 8'bz;  // Controlled_Buffer controlled_buffer_2
  and and_6 (and_6_out, sel_x, r);
  assign g_out = and_7_out ? rB_q : 8'bz;  // Controlled_Buffer controlled_buffer_3
  and and_7 (and_7_out, sel_b, r);
  assign g_out = and_8_out ? rA_q : 8'bz;  // Controlled_Buffer controlled_buffer_4
  and and_8 (and_8_out, sel_a, r);
endmodule

module SRF (
  input  r,
  input  w,
  input  INC_sel,
  input  INC_sel_ipl,
  input  [7:0] IP_INC_ip8_out,
  input  [7:0] s_in,
  input  sel_iph,
  input  sel_ipl,
  input  sel_sph,
  input  sel_spl,
  input  RAM_r,
  input  [7:0] RAM_d_out,
  input  sel_md,
  input  clock,
  output [7:0] s_out,
  output [7:0] IP_INC_ip8_in,
  output [7:0] CU_md
);

  wire and_1_out, and_2_out, and_3_out, and_4_out, and_5_out, and_6_out, and_7_out, and_8_out, and_9_out,
       and_10_out, or_1_out, or_2_out, or_3_out;
  wire [7:0] multiplexer_1_out, multiplexer_2_out, multiplexer_3_out, rIPH_q, rIPL_q, rSPH_q, rSPL_q;

  Multiplexer #(.width(8)) multiplexer_1 (.in0(s_in), .in1(IP_INC_ip8_out), .out(multiplexer_1_out), .sel(INC_sel));
  and and_1 (and_1_out, w, sel_iph);
  Multiplexer #(.width(8)) multiplexer_2 (.in0(s_in), .in1(IP_INC_ip8_out), .out(multiplexer_2_out), .sel(INC_sel_ipl));
  or or_1 (or_1_out, INC_sel_ipl, and_2_out);
  and and_2 (and_2_out, w, sel_ipl);
  and and_3 (and_3_out, w, sel_sph);
  and and_4 (and_4_out, w, sel_spl);
  Multiplexer #(.width(8)) multiplexer_3 (.in0(s_in), .in1(RAM_d_out), .out(multiplexer_3_out), .sel(RAM_r));
  or or_2 (or_2_out, RAM_r, and_5_out);
  and and_5 (and_5_out, w, sel_md);
  Register #(.trigger("high")) rIPH (.D(multiplexer_1_out), .en(or_3_out), .Q(rIPH_q), .clk(clock));  // open: clr
  or or_3 (or_3_out, and_1_out, INC_sel);
  Register #(.trigger("high")) rIPL (.D(multiplexer_2_out), .en(or_1_out), .Q(rIPL_q), .clk(clock));  // open: clr
  Register #(.trigger("high")) rSPH (.D(s_in), .en(and_3_out), .Q(rSPH_q), .clk(clock));  // open: clr
  Register #(.trigger("high")) rSPL (.D(s_in), .en(and_4_out), .Q(rSPL_q), .clk(clock));  // open: clr
  Register #(.trigger("high")) rMD (.D(multiplexer_3_out), .en(or_2_out), .Q(CU_md), .clk(clock));  // open: clr
  assign IP_INC_ip8_in = INC_sel ? rIPH_q : 8'bz;  // Controlled_Buffer controlled_buffer_1
  assign s_out = and_6_out ? rIPH_q : 8'bz;  // Controlled_Buffer controlled_buffer_2
  and and_6 (and_6_out, sel_iph, r);
  assign IP_INC_ip8_in = INC_sel_ipl ? rIPL_q : 8'bz;  // Controlled_Buffer controlled_buffer_3
  assign s_out = and_7_out ? rIPL_q : 8'bz;  // Controlled_Buffer controlled_buffer_4
  and and_7 (and_7_out, sel_ipl, r);
  assign s_out = and_8_out ? rSPH_q : 8'bz;  // Controlled_Buffer controlled_buffer_5
  and and_8 (and_8_out, sel_sph, r);
  assign s_out = and_9_out ? rSPL_q : 8'bz;  // Controlled_Buffer controlled_buffer_6
  and and_9 (and_9_out, sel_spl, r);
  assign s_out = and_10_out ? CU_md : 8'bz;  // Controlled_Buffer controlled_buffer_7
  and and_10 (and_10_out, sel_md, r);
  Pull_Resistor pull_resistor_1 (.node(CU_md));
endmodule

module IP_INC (
  input  sel_ipl,
  input  sel_iph,
  input  [7:0] ip8_in,
  input  clock,
  output [7:0] ip8_out
);

  wire adder_1_cout, and_1_out, d_ff_1_q;
  wire [7:0] pull_resistor_1_node;

  Pull_Resistor pull_resistor_1 (.node(pull_resistor_1_node));
  assign pull_resistor_1_node = sel_ipl ? 8'h1 : 8'bz;  // Controlled_Buffer controlled_buffer_1
  and and_1 (and_1_out, sel_iph, d_ff_1_q);
  Adder adder_1 (.a(ip8_in), .b(pull_resistor_1_node), .out(ip8_out), .cin(and_1_out), .cout(adder_1_cout));
  D_Flip_Flop d_ff_1 (.clk(clock), .D(adder_1_cout), .Q(d_ff_1_q));  // open: Qn, preset, reset
endmodule

module rTMP (
  input  wg,
  input  rg,
  input  ws,
  input  rs,
  input  wa,
  input  [7:0] g_in,
  input  [7:0] s_in,
  input  [7:0] ALU_res,
  input  clock,
  output [7:0] ALU_btmp,
  output [7:0] s_out,
  output [7:0] g_out
);

  wire or_1_out;
  wire [7:0] controlled_buffer_1_out;

  assign controlled_buffer_1_out = wa ? ALU_res : 8'bz;  // Controlled_Buffer controlled_buffer_1
  assign controlled_buffer_1_out = wg ? g_in : 8'bz;  // Controlled_Buffer controlled_buffer_2
  assign controlled_buffer_1_out = ws ? s_in : 8'bz;  // Controlled_Buffer controlled_buffer_3
  or or_1 (or_1_out, wg, ws, wa);
  Register TMP (.D(controlled_buffer_1_out), .en(or_1_out), .Q(ALU_btmp), .clk(clock));  // open: clr
  assign s_out = rs ? ALU_btmp : 8'bz;  // Controlled_Buffer controlled_buffer_4
  assign g_out = rg ? ALU_btmp : 8'bz;  // Controlled_Buffer controlled_buffer_5
endmodule

module ALU (
  input  asel,
  input  [7:0] ag,
  input  [7:0] as,
  input  cf_in,
  input  inv,
  input  [7:0] btmp,
  input  [7:0] bs,
  input  bsel,
  input  \and ,
  input  add,
  input  pb,
  input  pa,
  input  pbtoah,
  input  asr,
  input  lsl,
  output [7:0] res,
  output [7:0] adrl,
  output FLAGS_zf_in,
  output FLAGS_nf_in,
  output FLAGS_cf_in,
  output [7:0] adrh
);

  wire nor_1_out;
  wire [7:0] adder_1_out, and_1_out, bit_extender_1_out, controlled_buffer_1_out, controlled_buffer_2_out,
       controlled_buffer_3_out, controlled_buffer_6_out, controlled_buffer_7_out, controlled_buffer_8_out,
       multiplexer_1_out, multiplexer_2_out, or_1_out, pull_resistor_1_node, xor_1_out;

  Multiplexer #(.width(8)) multiplexer_1 (.in0(ag), .in1(as), .out(multiplexer_1_out), .sel(asel));
  Multiplexer #(.width(8)) multiplexer_2 (.in0(btmp), .in1(bs), .out(multiplexer_2_out), .sel(bsel));
  assign xor_1_out = multiplexer_1_out ^ bit_extender_1_out;  // XOR_Gate xor_1, 8 bits wide
  assign bit_extender_1_out = {{7{inv}}, inv};  // Bit_Extender bit_extender_1
  assign controlled_buffer_1_out = pb ? multiplexer_2_out : 8'bz;  // Controlled_Buffer controlled_buffer_1
  assign controlled_buffer_2_out = add ? adder_1_out : 8'bz;  // Controlled_Buffer controlled_buffer_2
  Adder adder_1 (.a(xor_1_out), .b(multiplexer_2_out), .out(adder_1_out), .cin(cf_in), .cout(FLAGS_cf_in));
  assign and_1_out = xor_1_out & multiplexer_2_out;  // AND_Gate and_1, 8 bits wide
  assign controlled_buffer_3_out = \and  ? and_1_out : 8'bz;  // Controlled_Buffer controlled_buffer_3
  Pull_Resistor pull_resistor_1 (.node(pull_resistor_1_node));
  assign pull_resistor_1_node = pa ? xor_1_out : 8'bz;  // Controlled_Buffer controlled_buffer_4
  Pull_Resistor pull_resistor_2 (.node(controlled_buffer_1_out));
  Pull_Resistor pull_resistor_3 (.node(controlled_buffer_2_out));
  Pull_Resistor pull_resistor_4 (.node(controlled_buffer_3_out));
  assign adrh = pbtoah ? multiplexer_2_out : 8'bz;  // Controlled_Buffer controlled_buffer_5
  assign or_1_out = pull_resistor_1_node | controlled_buffer_1_out | controlled_buffer_2_out | controlled_buffer_3_out;  // OR_Gate or_1, 8 bits wide
  Pull_Resistor pull_resistor_5 (.node(adrh));
  assign controlled_buffer_6_out = lsl ? {or_1_out[6:0], 1'b0} : 8'bz;  // Controlled_Buffer controlled_buffer_6
  assign controlled_buffer_7_out = nor_1_out ? or_1_out : 8'bz;  // Controlled_Buffer controlled_buffer_7
  assign controlled_buffer_8_out = asr ? {{2{or_1_out[7]}}, or_1_out[6:1]} : 8'bz;  // Controlled_Buffer controlled_buffer_8
  nor nor_1 (nor_1_out, lsl, asr);
  Pull_Resistor pull_resistor_6 (.node(controlled_buffer_6_out));
  assign adrl = controlled_buffer_6_out | controlled_buffer_7_out | controlled_buffer_8_out;  // OR_Gate or_2, 8 bits wide
  Pull_Resistor pull_resistor_7 (.node(controlled_buffer_7_out));
  Pull_Resistor pull_resistor_8 (.node(controlled_buffer_8_out));
  nor nor_2 (FLAGS_zf_in, adrl[0], adrl[1], adrl[2], adrl[3], adrl[4], adrl[5], adrl[6], adrl[7]);

  assign FLAGS_nf_in = adrl[7];
  assign res = adrl;

  // Notes on the sheet:
  //   Left logic shift
  //   Right arithmetic shift
endmodule

module SF (
  input  wcf,
  input  wzf,
  input  wnf,
  input  sel,
  input  cf_in,
  input  zf_in,
  input  nf_in,
  input  clock,
  output cf_out,
  output zf_out,
  output nf_out
);

  wire and_1_out, and_2_out, and_3_out, C_q, N_q, Z_q;

  D_Flip_Flop #(.trigger("high")) C (.clk(clock), .D(cf_in), .Q(C_q));  // open: Qn, preset, reset
  and and_1 (and_1_out, wcf, sel);
  D_Flip_Flop #(.trigger("high")) Z (.clk(clock), .D(zf_in), .Q(Z_q));  // open: Qn, preset, reset
  and and_2 (and_2_out, wzf, sel);
  D_Flip_Flop #(.trigger("high")) N (.clk(clock), .D(nf_in), .Q(N_q));  // open: Qn, preset, reset
  and and_3 (and_3_out, wnf, sel);
  assign cf_out = sel ? C_q : 1'bz;  // Controlled_Buffer controlled_buffer_1
  assign zf_out = sel ? Z_q : 1'bz;  // Controlled_Buffer controlled_buffer_2
  assign nf_out = sel ? N_q : 1'bz;  // Controlled_Buffer controlled_buffer_3
endmodule

module GF (
  input  wcf,
  input  wzf,
  input  wnf,
  input  wif,
  input  sel,
  input  cf_in,
  input  zf_in,
  input  nf_in,
  input  if_in,
  input  clock,
  output cf_out,
  output zf_out,
  output nf_out,
  output if_out
);

  wire and_1_out, and_2_out, and_3_out, and_4_out, C_q, I_q, N_q, Z_q;

  D_Flip_Flop #(.trigger("high")) C (.clk(clock), .D(cf_in), .Q(C_q));  // open: Qn, preset, reset
  and and_1 (and_1_out, wcf, sel);
  D_Flip_Flop #(.trigger("high")) Z (.clk(clock), .D(zf_in), .Q(Z_q));  // open: Qn, preset, reset
  and and_2 (and_2_out, wzf, sel);
  D_Flip_Flop #(.trigger("high")) N (.clk(clock), .D(nf_in), .Q(N_q));  // open: Qn, preset, reset
  and and_3 (and_3_out, wnf, sel);
  D_Flip_Flop #(.trigger("high")) I (.clk(clock), .D(if_in), .Q(I_q));  // open: Qn, preset, reset
  and and_4 (and_4_out, wif, sel);
  assign cf_out = sel ? C_q : 1'bz;  // Controlled_Buffer controlled_buffer_1
  assign zf_out = sel ? Z_q : 1'bz;  // Controlled_Buffer controlled_buffer_2
  assign nf_out = sel ? N_q : 1'bz;  // Controlled_Buffer controlled_buffer_3
  assign if_out = sel ? I_q : 1'bz;  // Controlled_Buffer controlled_buffer_4
endmodule

module FLAGS (
  input  ws,
  input  rsel,
  input  [7:0] g,
  input  cf_in,
  input  nf_in,
  input  zf_in,
  input  if_in,
  input  wif,
  input  wnf,
  input  wzf,
  input  wcf,
  input  clock,
  output if_out,
  output nf_out,
  output zf_out,
  output cf_out
);

  wire decoder_1_out0, decoder_1_out1, decoder_2_out0, decoder_2_out1;
  wire [3:0] controlled_buffer_1_out;

  Decoder #(.enable("false")) decoder_1 (.out0(decoder_1_out0), .out1(decoder_1_out1), .sel(ws));
  assign controlled_buffer_1_out = decoder_1_out1 ? g[3:0] : 4'bz;  // Controlled_Buffer controlled_buffer_1
  assign controlled_buffer_1_out[0] = decoder_1_out0 ? cf_in : 1'bz;  // Controlled_Buffer controlled_buffer_2
  assign controlled_buffer_1_out[1] = decoder_1_out0 ? nf_in : 1'bz;  // Controlled_Buffer controlled_buffer_3
  assign controlled_buffer_1_out[2] = decoder_1_out0 ? zf_in : 1'bz;  // Controlled_Buffer controlled_buffer_4
  assign controlled_buffer_1_out[3] = decoder_1_out0 ? if_in : 1'bz;  // Controlled_Buffer controlled_buffer_5
  Decoder #(.enable("false")) decoder_2 (.out0(decoder_2_out0), .out1(decoder_2_out1), .sel(rsel));
  SF sf_1 (
    .cf_out(cf_out), .zf_out(zf_out), .nf_out(nf_out), .wzf(wzf), .wnf(wnf), .sel(decoder_2_out1),
    .cf_in(controlled_buffer_1_out[0]), .zf_in(controlled_buffer_1_out[1]),
    .nf_in(controlled_buffer_1_out[2]), .wcf(wcf), .clock(clock));
  GF gf_1 (
    .cf_out(cf_out), .zf_out(zf_out), .nf_out(nf_out), .if_out(if_out), .wnf(wnf), .wif(wif),
    .sel(decoder_2_out0), .cf_in(controlled_buffer_1_out[0]), .zf_in(controlled_buffer_1_out[1]),
    .nf_in(controlled_buffer_1_out[2]), .if_in(controlled_buffer_1_out[3]), .wcf(wcf), .wzf(wzf),
    .clock(clock));
endmodule

module MID (
  input  [55:0] mi,
  output SRF_sel_iph,
  output SRF_sel_ipl,
  output SRF_sel_sph,
  output SRF_sel_spl,
  output SRF_sel_md,
  output SRF_r,
  output SRF_w,
  output RAM_r,
  output RAM_w,
  output IP_INC_sel_iph,
  output IP_INC_sel_ipl,
  output FLAGS_rsel,
  output FLAGS_ws,
  output FLAGS_if_in,
  output CU_wcf,
  output FLAGS_wcf,
  output CU_wzf,
  output FLAGS_wzf,
  output CU_wnf,
  output FLAGS_wnf,
  output CU_wif,
  output FLAGS_wif,
  output ALU_bsel,
  output ALU_add,
  output ALU_and,
  output ALU_inv,
  output ALU_asel,
  output ALU_pbtoah,
  output ALU_pb,
  output ALU_pa,
  output ALU_asr,
  output ALU_lsl,
  output rTMP_wg,
  output rTMP_rg,
  output rTMP_ws,
  output rTMP_rs,
  output rTMP_wa,
  output GRF_w,
  output GRF_r,
  output GRF_sel_y,
  output GRF_sel_x,
  output GRF_sel_b,
  output GRF_sel_a,
  output CU_cnd,
  output CU_wmd,
  output [11:0] CU_nmip
);


  assign ALU_add = mi[19];
  assign ALU_and = mi[20];
  assign ALU_asel = mi[22];
  assign ALU_asr = mi[26];
  assign ALU_bsel = mi[18];
  assign ALU_inv = mi[21];
  assign ALU_lsl = mi[27];
  assign ALU_pa = mi[25];
  assign ALU_pb = mi[24];
  assign ALU_pbtoah = mi[23];
  assign CU_cnd = mi[39];
  assign CU_nmip = mi[55:44];
  assign CU_wcf = mi[14];
  assign CU_wif = mi[17];
  assign CU_wmd = mi[40];
  assign CU_wnf = mi[16];
  assign CU_wzf = mi[15];
  assign FLAGS_if_in = mi[13];
  assign FLAGS_rsel = mi[11];
  assign FLAGS_wcf = mi[14];
  assign FLAGS_wif = mi[17];
  assign FLAGS_wnf = mi[16];
  assign FLAGS_ws = mi[12];
  assign FLAGS_wzf = mi[15];
  assign GRF_r = mi[34];
  assign GRF_sel_a = mi[38];
  assign GRF_sel_b = mi[37];
  assign GRF_sel_x = mi[36];
  assign GRF_sel_y = mi[35];
  assign GRF_w = mi[33];
  assign IP_INC_sel_iph = mi[9];
  assign IP_INC_sel_ipl = mi[10];
  assign RAM_r = mi[7];
  assign RAM_w = mi[8];
  assign rTMP_rg = mi[29];
  assign rTMP_rs = mi[31];
  assign rTMP_wa = mi[32];
  assign rTMP_wg = mi[28];
  assign rTMP_ws = mi[30];
  assign SRF_r = mi[5];
  assign SRF_sel_iph = mi[0];
  assign SRF_sel_ipl = mi[1];
  assign SRF_sel_md = mi[4];
  assign SRF_sel_sph = mi[2];
  assign SRF_sel_spl = mi[3];
  assign SRF_w = mi[6];
endmodule

module MC_ROM (
  input  [11:0] adr,
  output [55:0] mi
);

  wire [55:0] rom_1_data, rom_2_data;

  ROM #(.addrWidth(12), .dataWidth(56)) rom_1 (.addr(adr), .data(rom_1_data));
  ROM #(.addrWidth(12)) rom_2 (.addr(adr), .data(rom_2_data[7:0]));
  ROM #(.addrWidth(12)) rom_3 (.addr(adr), .data(rom_2_data[15:8]));
  ROM #(.addrWidth(12)) rom_4 (.addr(adr), .data(rom_2_data[23:16]));
  ROM #(.addrWidth(12)) rom_5 (.addr(adr), .data(rom_2_data[31:24]));
  ROM #(.addrWidth(12)) rom_6 (.addr(adr), .data(rom_2_data[39:32]));
  ROM #(.addrWidth(12)) rom_7 (.addr(adr), .data(rom_2_data[47:40]));
  ROM #(.addrWidth(12)) rom_8 (.addr(adr), .data(rom_2_data[55:48]));
  Multiplexer #(.width(56)) multiplexer_1 (.in0(rom_1_data), .in1(rom_2_data), .out(mi), .sel(1'b0));

  // Notes on the sheet:
  //   byte 0
  //   contents of rom_3 (hex, n*v repeats v):
  //   24 94*0 34 5*0 34
  //   byte 1
  //   byte 2
  //   byte 3
  //   byte 4
  //   byte 5
  //   byte 6
  //   select_8bit_roms
endmodule

module CU (
  input  [55:0] MC_ROM_mi,
  input  wcf,
  input  wzf,
  input  wnf,
  input  wif,
  input  cnd,
  input  FLAGS_cf_out,
  input  FLAGS_zf_out,
  input  FLAGS_nf_out,
  input  FLAGS_if_out,
  input  i,
  input  sel_adr,
  input  [11:0] nmip,
  input  [7:0] md,
  input  clock,
  output [55:0] MID_mi,
  output [11:0] MC_ROM_adr
);

  wire and_1_out, and_2_out, and_3_out, and_4_out, and_5_out, and_6_out, decoder_1_out0, decoder_1_out1,
       not_1_out, or_1_out;
  wire [11:0] bit_extender_1_out, controlled_buffer_1_out, xor_1_out;

  not not_1 (not_1_out, and_5_out);
  Decoder decoder_1 (.out0(decoder_1_out0), .out1(decoder_1_out1), .sel(sel_adr), .en(not_1_out));
  assign controlled_buffer_1_out = decoder_1_out1 ? nmip : 12'bz;  // Controlled_Buffer controlled_buffer_1
  and and_1 (and_1_out, wcf, FLAGS_cf_out);
  and and_2 (and_2_out, wzf, FLAGS_zf_out);
  and and_3 (and_3_out, wnf, FLAGS_nf_out);
  and and_4 (and_4_out, wif, FLAGS_if_out);
  and and_5 (and_5_out, FLAGS_if_out, i);
  assign controlled_buffer_1_out = decoder_1_out0 ? {md, 4'b0000} : 12'bz;  // Controlled_Buffer controlled_buffer_2
  or or_1 (or_1_out, and_1_out, and_2_out, and_3_out, and_4_out);
  assign controlled_buffer_1_out = and_5_out ? {12{1'b0}} : 12'bz;  // Controlled_Buffer controlled_buffer_3
  and and_6 (and_6_out, or_1_out, cnd);
  Register #(.width(28)) register_1 (.D(MC_ROM_mi[27:0]), .Q(MID_mi[27:0]), .clk(clock));  // open: en, clr
  Register #(.width(28)) register_2 (.D(MC_ROM_mi[55:28]), .Q(MID_mi[55:28]), .clk(clock));  // open: en, clr
  assign bit_extender_1_out = {{11{1'b0}}, and_6_out};  // Bit_Extender bit_extender_1
  assign xor_1_out = bit_extender_1_out ^ controlled_buffer_1_out;  // XOR_Gate xor_1, 12 bits wide
  Register #(.trigger("high"), .width(12)) MIP (.D(xor_1_out), .Q(MC_ROM_adr), .clk(clock));  // open: en, clr

  // Notes on the sheet:
  //   int_mi_adr
  //   SR
endmodule
